# Fritzing sketch Schéma Fritzing Projet - Groupe 5 (saved by Fritzing 0.9.3b)
breadboards: 1

parts:
  Composant1 = Arduino Uno (Rev3)
  L1 = Inductor [inductance=10mH package="400 mil [THT]"]
  C1 = Tantalum Capacitor [capacitance=1μF package="100 mil [THT, tantalum]"]
  D1 = Rectifier Diode [part_number=1N4001 package="300 mil [THT]"]
  R2 = Resistor [tolerance=±5% resistance=1M package=THT]
  R1 = Resistor [tolerance=±5% resistance=10k package=THT]
  R3 = Resistor [tolerance=±5% resistance=3.3k package=THT]
  C2 = Ceramic Capacitor [capacitance=0.1nF package="100 mil [THT, multilayer]"]
  R4 = Resistor [tolerance=±5% resistance=220 package=THT]
  LED1 = LED - 3mm [color="Green (555nm)" package="3 mm [THT]"]
  R5 = Resistor [tolerance=±5% resistance=220 package=THT]
  LED2 = LED - 3mm [color="Yellow (585nm)" package="3 mm [THT]"]
  R6 = Resistor [tolerance=±5% resistance=220 package=THT]
  LED3 = LED - 3mm [color="Red (633nm)" package="3 mm [THT]"]

nets:
  N1: Composant1.A0, L1.pin_0, C1.+, D1.cathode, D1.anode, R2.Pin_0, R2.Pin_1, C2.0
  N2: Composant1.D9_PWM, R1.Pin_1
  N3: Composant1.D2, R4.Pin_0
  N4: Composant1.D4, R5.Pin_0
  N5: Composant1.D7, R6.Pin_0
  N6: L1.pin_1, R1.Pin_0, R3.Pin_1
  N7: R3.Pin_0, C2.1, LED1.anode, LED2.anode, LED3.anode
  N8: R4.Pin_1, LED1.cathode
  N9: R5.Pin_1, LED2.cathode
  N10: R6.Pin_1, LED3.cathode
